// Logisim project P3_L0_2022.circ as structural Verilog: 10 circuits, main circuit main
module main (
  input  reset,
  output [31:0] Instr,
  output RegWrite,
  output [4:0] RegAddr,
  output [31:0] RegData,
  output MemWrite,
  output [4:0] MemAddr,
  output [31:0] MemData
);

  wire beq, bit_extender_1_out, lui, lw, lw_sw, MemWrite_t, ori, R_I, RegWrite_t;
  wire [2:0] ALU_op;
  wire [4:0] Rd, RegAdr, Rs, Rt, shamt;
  wire [5:0] func, spilitter_1_op;
  wire [6:0] MemAddr_Byte;
  wire [15:0] imm;
  wire [25:0] j_address;
  wire [31:0] adder_1_out, adder_2_out, ALU_output, bit_extender_2_out, bit_extender_3_out, DM_output,
       grf_1_rd1, Instr_t, MemData_t, multiplexer_2_out, multiplexer_4_out, multiplexer_5_out,
       multiplexer_6_out, multiplexer_7_out, PC, RegData_t, signed_ext_2_1_ext_output, undriven,
       zero_ext_16_1_out_2;

  Adder #(.width(32)) adder_1 (.a(32'h4), .b(PC), .out(adder_1_out));  // open: cin, cout
  signed_EXT_2 signed_ext_2_1 (.EXT_input(imm), .EXT_output(signed_ext_2_1_ext_output));
  Multiplexer #(.width(5), .enable("false")) multiplexer_1 (.in0(Rd), .in1(Rt), .out(RegAdr), .sel(R_I));
  Multiplexer #(.width(32)) multiplexer_2 (
    .in0(ALU_output), .in1(DM_output), .out(multiplexer_2_out), .sel(lw));  // open: en
  zero_EXT_16 zero_ext_16_1 (.in_1(imm), .out_2(zero_ext_16_1_out_2));
  Adder #(.width(32)) adder_2 (.a(adder_1_out), .b(signed_ext_2_1_ext_output), .out(adder_2_out));  // open: cin, cout
  Multiplexer #(.width(32), .enable("false")) multiplexer_3 (
    .in0(multiplexer_2_out), .in1(zero_ext_16_1_out_2), .out(RegData_t), .sel(lui));
  Multiplexer #(.width(32)) multiplexer_4 (
    .in0(adder_2_out), .in1(adder_1_out), .out(multiplexer_4_out), .sel(bit_extender_1_out));  // open: en
  Bit_Extender #(.in_width(32), .out_width(1)) bit_extender_1 (.in(ALU_output), .out(bit_extender_1_out));
  GRF grf_1 (
    .reset(reset), .RegWrite(RegWrite_t), .A1(Rs), .A2(Rt), .RegAddr(RegAdr), .RegData(RegData_t),
    .RD1(grf_1_rd1), .RD2(MemData_t));
  // Probe on RegData_t
  Multiplexer #(.select(2), .width(32)) multiplexer_5 (
    .in0(adder_1_out), .in1(multiplexer_4_out), .in2(undriven), .out(multiplexer_5_out), .sel({1'b0, beq}));  // open: in3, en
  assign bit_extender_2_out = {{16{imm[15]}}, imm};  // Bit_Extender bit_extender_2
  // Probe on PC
  // Probe on multiplexer_5_out
  Multiplexer #(.width(32), .enable("false")) multiplexer_6 (
    .in0(MemData_t), .in1(bit_extender_2_out), .out(multiplexer_6_out), .sel(lw_sw));
  IFU ifu_1 (.next_PC(multiplexer_5_out), .Instr(Instr_t), .PC(PC), .reset(reset));
  Multiplexer #(.width(32), .enable("false")) multiplexer_7 (
    .in0(multiplexer_6_out), .in1(bit_extender_3_out), .out(multiplexer_7_out), .sel(ori));
  assign bit_extender_3_out = {{16{1'b0}}, imm};  // Bit_Extender bit_extender_3
  OUTPUT output_1 (
    .Instr(Instr_t), .RegWrite(RegWrite_t), .RegAdr(RegAdr), .RegData(RegData_t), .MemWrite(MemWrite_t),
    .MemAddr_Byte(MemAddr_Byte), .MemData(MemData_t), .Instr_2(Instr), .RegWrite_2(RegWrite),
    .RegAddr(RegAddr), .RegData_2(RegData), .MemWrite_2(MemWrite), .MemAddr(MemAddr), .MemData_2(MemData));
  spilitter spilitter_1 (
    .instruction(Instr_t), .func(func), .shamt(shamt), .Rd(Rd), .Rt(Rt), .Rs(Rs), .op(spilitter_1_op),
    .imm_16(imm), .j_address_26(j_address));
  controller controller_1 (
    .op(spilitter_1_op), .func(func), .R_I(R_I), .RegWrite(RegWrite_t), .lw_or_sw(lw_sw),
    .MemWrite(MemWrite_t), .beq_control(beq), .lui_control(lui), .ori_control(ori), .lw_control(lw),
    .ALU_op(ALU_op));
  Bit_Extender #(.in_width(32), .out_width(7)) bit_extender_4 (.in(ALU_output), .out(MemAddr_Byte));
  ALU alu_1 (.a(grf_1_rd1), .b(multiplexer_7_out), .ALU_op(ALU_op), .ans(ALU_output));
  DM dm_1 (.MemAddr(MemAddr_Byte), .MemData(MemData_t), .MemWrite(MemWrite_t), .MemOut(DM_output), .reset(reset));

  // Other names for the same wires on the sheet: RD2[31:0] = MemData_t
endmodule

module controller (
  input  [5:0] op,
  input  [5:0] func,
  output R_I,
  output RegWrite,
  output lw_or_sw,
  output MemWrite,
  output beq_control,
  output lui_control,
  output ori_control,
  output lw_control,
  output [2:0] ALU_op
);

  wire add_out, beq_out, func_add, func_sub, lui_out, lw_out, ori_out, sub_out, sw_out;
  wire [2:0] multiplexer_1_out, multiplexer_2_out, multiplexer_3_out, multiplexer_4_out, multiplexer_5_out,
       multiplexer_6_out;

  and add (add_out, ~op[5], ~op[4], ~op[3], ~op[2], ~op[1], ~op[0], func_add);  // AND_Gate
  and sub (sub_out, ~op[5], ~op[4], ~op[3], ~op[2], ~op[1], ~op[0], func_sub);  // AND_Gate
  Multiplexer #(.width(3), .disabled(0)) multiplexer_1 (
    .in0(3'b000), .in1(3'b000), .out(multiplexer_1_out), .sel(add_out));  // open: en
  and ori (ori_out, ~op[5], ~op[4], op[3], op[2], ~op[1], op[0]);  // AND_Gate
  Multiplexer #(.width(3), .disabled(0)) multiplexer_2 (
    .in0(3'b000), .in1(3'b001), .out(multiplexer_2_out), .sel(sub_out));  // open: en
  and lw (lw_out, op[5], ~op[4], ~op[3], ~op[2], op[1], op[0]);  // AND_Gate
  Multiplexer #(.width(3), .disabled(0)) multiplexer_3 (
    .in0(3'b000), .in1(3'b010), .out(multiplexer_3_out), .sel(ori_out));  // open: en
  and sw (sw_out, op[5], ~op[4], op[3], ~op[2], op[1], op[0]);  // AND_Gate
  Multiplexer #(.width(3), .disabled(0)) multiplexer_4 (
    .in0(3'b000), .in1(3'b000), .out(multiplexer_4_out), .sel(lw_out));  // open: en
  and beq (beq_out, ~op[5], ~op[4], ~op[3], op[2], ~op[1], ~op[0]);  // AND_Gate
  Multiplexer #(.width(3), .disabled(0)) multiplexer_5 (
    .in0(3'b000), .in1(3'b000), .out(multiplexer_5_out), .sel(sw_out));  // open: en
  and lui (lui_out, ~op[5], ~op[4], op[3], op[2], op[1], op[0]);  // AND_Gate
  Multiplexer #(.width(3), .disabled(0)) multiplexer_6 (
    .in0(3'b000), .in1(3'b011), .out(multiplexer_6_out), .sel(beq_out));  // open: en
  and u_func_add (func_add, func[5], ~func[4], ~func[3], ~func[2], ~func[1], ~func[0]);  // AND_Gate
  and func_add_2 (func_sub, func[5], ~func[4], ~func[3], ~func[2], func[1], ~func[0]);  // AND_Gate
  or u_R_I (R_I, ori_out, lw_out, lui_out);
  or u_RegWrite (RegWrite, add_out, sub_out, ori_out, lw_out, lui_out);
  or u_lw_or_sw (lw_or_sw, lw_out, sw_out);
  buf u_MemWrite (MemWrite, sw_out);  // OR_Gate
  buf u_beq_control (beq_control, beq_out);  // OR_Gate
  buf u_lui_control (lui_control, lui_out);  // OR_Gate
  buf u_ori_control (ori_control, ori_out);  // OR_Gate
  buf u_lw_control (lw_control, lw_out);  // OR_Gate
  assign ALU_op = multiplexer_1_out | multiplexer_2_out | multiplexer_3_out | multiplexer_4_out | multiplexer_5_out | multiplexer_6_out;  // OR_Gate ALU_op, 3 bits wide
endmodule

module spilitter (
  input  [31:0] instruction,
  output [5:0] func,
  output [4:0] shamt,
  output [4:0] Rd,
  output [4:0] Rt,
  output [4:0] Rs,
  output [5:0] op,
  output [15:0] imm_16,
  output [25:0] j_address_26
);


  assign func = instruction[5:0];
  assign imm_16 = instruction[15:0];
  assign j_address_26 = instruction[25:0];
  assign op = instruction[31:26];
  assign Rd = instruction[15:11];
  assign Rs = instruction[25:21];
  assign Rt = instruction[20:16];
  assign shamt = instruction[10:6];
endmodule

module IFU (
  input  [31:0] next_PC,
  input  reset,
  output [31:0] PC,
  output [31:0] Instr
);

  wire clock_1_out;
  wire [9:0] bit_extender_1_out;
  wire [31:0] shifter_1_out;

  Clock clock_1 (.out(clock_1_out));
  Register #(.width(32)) u_PC (.D(next_PC), .Q(PC), .clk(clock_1_out), .clr(reset));  // open: en
  Shifter #(.width(32), .shift("lr")) shifter_1 (.in(PC), .\dist (5'b00010), .out(shifter_1_out));
  Bit_Extender #(.in_width(32), .out_width(10)) bit_extender_1 (.in(shifter_1_out), .out(bit_extender_1_out));
  ROM #(.addrWidth(10), .dataWidth(32)) rom_1 (.addr(bit_extender_1_out), .data(Instr));  // open: sel

  // Notes on the sheet:
  //   contents of rom_1 (hex, n*v repeats v):
  //   3404007b 348501c8 3c06007b 3c07ffff 34e7ffff 868020 878820 e79020 34080000 ad040000 ad050004
  //   ad060008 ad07000c ad100010 ad110014 ad120018 8d040000 8d05000c ad04001c ad050020 34040001 34050002
  //   34060001 10850001 10860001 ad040024 ad050028
endmodule

module GRF (
  input  reset,
  input  RegWrite,
  input  [4:0] A1,
  input  [4:0] A2,
  input  [4:0] RegAddr,
  input  [31:0] RegData,
  output [31:0] RD1,
  output [31:0] RD2
);

  wire clk, en0, en1, en2, en3, en4, en5, en6, en7, en8, en9, en10, en11, en12, en13, en14, en15, en16, en17,
       en18, en19, en20, en21, en22, en23, en24, en25, en26, en27, en28, en29, en30, en31;
  wire [31:0] in0, in1, in2, in3, in4, in5, in6, in7, in8, in9, in10, in11, in12, in13, in14, in15, in16,
       in17, in18, in19, in20, in21, in22, in23, in24, in25, in26, in27, in28, in29, in30, in31, out0, out1,
       out2, out3, out4, out5, out6, out7, out8, out9, out10, out11, out12, out13, out14, out15, out16,
       out17, out18, out19, out20, out21, out22, out23, out24, out25, out26, out27, out28, out29, out30,
       out31;

  Clock u_clk (.out(clk));
  Demultiplexer #(.select(5), .width(32), .tristate("true")) demultiplexer_1 (
    .out1(in1), .out2(in2), .out3(in3), .out4(in4), .out5(in5), .out6(in6), .out7(in7), .out8(in8),
    .out9(in9), .out10(in10), .out11(in11), .out12(in12), .out13(in13), .out14(in14), .out15(in15),
    .out16(in16), .out17(in17), .out18(in18), .out19(in19), .out20(in20), .out21(in21), .out22(in22),
    .out23(in23), .out24(in24), .out25(in25), .out26(in26), .out27(in27), .out28(in28), .out29(in29),
    .out30(in30), .out31(in31), .in(RegData), .sel(RegAddr), .en(RegWrite));  // open: out0
  Register #(.width(32)) reg0 (.D(in0), .en(en0), .Q(out0), .clk(clk), .clr(reset));
  Register #(.width(32)) reg1 (.D(in1), .en(en1), .Q(out1), .clk(clk), .clr(reset));
  Register #(.width(32)) reg2 (.D(in2), .en(en2), .Q(out2), .clk(clk), .clr(reset));
  Register #(.width(32)) reg3 (.D(in3), .en(en3), .Q(out3), .clk(clk), .clr(reset));
  Register #(.width(32)) reg4 (.D(in4), .en(en4), .Q(out4), .clk(clk), .clr(reset));
  Register #(.width(32)) reg5 (.D(in5), .en(en5), .Q(out5), .clk(clk), .clr(reset));
  Register #(.width(32)) reg6 (.D(in6), .en(en6), .Q(out6), .clk(clk), .clr(reset));
  Register #(.width(32)) reg7 (.D(in7), .en(en7), .Q(out7), .clk(clk), .clr(reset));
  Register #(.width(32)) reg8 (.D(in8), .en(en8), .Q(out8), .clk(clk), .clr(reset));
  Register #(.width(32)) reg9 (.D(in9), .en(en9), .Q(out9), .clk(clk), .clr(reset));
  Register #(.width(32)) reg10 (.D(in10), .en(en10), .Q(out10), .clk(clk), .clr(reset));
  Register #(.width(32)) reg11 (.D(in11), .en(en11), .Q(out11), .clk(clk), .clr(reset));
  Register #(.width(32)) reg12 (.D(in12), .en(en12), .Q(out12), .clk(clk), .clr(reset));
  Register #(.width(32)) reg13 (.D(in13), .en(en13), .Q(out13), .clk(clk), .clr(reset));
  Register #(.width(32)) reg14 (.D(in14), .en(en14), .Q(out14), .clk(clk), .clr(reset));
  Register #(.width(32)) reg15 (.D(in15), .en(en15), .Q(out15), .clk(clk), .clr(reset));
  Register #(.width(32)) reg16 (.D(in16), .en(en16), .Q(out16), .clk(clk), .clr(reset));
  Register #(.width(32)) reg17 (.D(in17), .en(en17), .Q(out17), .clk(clk), .clr(reset));
  Register #(.width(32)) reg18 (.D(in18), .en(en18), .Q(out18), .clk(clk), .clr(reset));
  Register #(.width(32)) reg19 (.D(in19), .en(en19), .Q(out19), .clk(clk), .clr(reset));
  Register #(.width(32)) reg20 (.D(in20), .en(en20), .Q(out20), .clk(clk), .clr(reset));
  Register #(.width(32)) reg21 (.D(in21), .en(en21), .Q(out21), .clk(clk), .clr(reset));
  Register #(.width(32)) reg22 (.D(in22), .en(en22), .Q(out22), .clk(clk), .clr(reset));
  Register #(.width(32)) reg23 (.D(in23), .en(en23), .Q(out23), .clk(clk), .clr(reset));
  Register #(.width(32)) reg24 (.D(in24), .en(en24), .Q(out24), .clk(clk), .clr(reset));
  Register #(.width(32)) reg25 (.D(in25), .en(en25), .Q(out25), .clk(clk), .clr(reset));
  Register #(.width(32)) reg26 (.D(in26), .en(en26), .Q(out26), .clk(clk), .clr(reset));
  Register #(.width(32)) reg27 (.D(in27), .en(en27), .Q(out27), .clk(clk), .clr(reset));
  Register #(.width(32)) reg28 (.D(in28), .en(en28), .Q(out28), .clk(clk), .clr(reset));
  Register #(.width(32)) reg29 (.D(in29), .en(en29), .Q(out29), .clk(clk), .clr(reset));
  Register #(.width(32)) reg30 (.D(in30), .en(en30), .Q(out30), .clk(clk), .clr(reset));
  Register #(.width(32)) reg31 (.D(in31), .en(en31), .Q(out31), .clk(clk), .clr(reset));
  Multiplexer #(.select(5), .width(32)) multiplexer_1 (
    .in0(out0), .in1(out1), .in2(out2), .in3(out3), .in4(out4), .in5(out5), .in6(out6), .in7(out7),
    .in8(out8), .in9(out9), .in10(out10), .in11(out11), .in12(out12), .in13(out13), .in14(out14),
    .in15(out15), .in16(out16), .in17(out17), .in18(out18), .in19(out19), .in20(out20), .in21(out21),
    .in22(out22), .in23(out23), .in24(out24), .in25(out25), .in26(out26), .in27(out27), .in28(out28),
    .in29(out29), .in30(out30), .in31(out31), .out(RD1), .sel(A1));  // open: en
  Multiplexer #(.select(5), .width(32)) multiplexer_2 (
    .in0(out0), .in1(out1), .in2(out2), .in3(out3), .in4(out4), .in5(out5), .in6(out6), .in7(out7),
    .in8(out8), .in9(out9), .in10(out10), .in11(out11), .in12(out12), .in13(out13), .in14(out14),
    .in15(out15), .in16(out16), .in17(out17), .in18(out18), .in19(out19), .in20(out20), .in21(out21),
    .in22(out22), .in23(out23), .in24(out24), .in25(out25), .in26(out26), .in27(out27), .in28(out28),
    .in29(out29), .in30(out30), .in31(out31), .out(RD2), .sel(A2));  // open: en
endmodule

module ALU (
  input  [31:0] a,
  input  [31:0] b,
  input  [2:0] ALU_op,
  output [31:0] ans
);

  wire [1:0] comparator_1_gt;
  wire [31:0] adder_1_out, multiplexer_1_out, or_1_out, subtractor_1_out;

  Comparator #(.width(32)) comparator_1 (.a(a), .b(b), .gt(comparator_1_gt[0]), .lt(comparator_1_gt[1]));  // open: eq
  Adder #(.width(32)) adder_1 (.a(a), .b(b), .out(adder_1_out));  // open: cin, cout
  Subtractor #(.width(32)) subtractor_1 (.a(a), .b(b), .out(subtractor_1_out));  // open: bin, bout
  assign or_1_out = a | b;  // OR_Gate or_1, 32 bits wide
  Multiplexer #(.select(2), .width(32), .enable("false")) multiplexer_1 (
    .in0({32{1'b0}}), .in1(32'h1), .in2(32'h11111111), .out(multiplexer_1_out), .sel(comparator_1_gt));  // open: in3
  Multiplexer #(.select(3), .width(32)) multiplexer_2 (
    .in0(adder_1_out), .in1(subtractor_1_out), .in2(or_1_out), .in3(multiplexer_1_out), .out(ans),
    .sel(ALU_op));  // open: in4, in5, in6, in7, en
endmodule

module DM (
  input  [6:0] MemAddr,
  input  [31:0] MemData,
  input  MemWrite,
  input  reset,
  output [31:0] MemOut
);

  wire clock_1_out, not_1_out;
  wire [4:0] bit_extender_1_out;
  wire [6:0] shifter_1_out;

  Shifter #(.width(7), .shift("lr")) shifter_1 (.in(MemAddr), .\dist (3'b010), .out(shifter_1_out));
  Bit_Extender #(.in_width(7), .out_width(5)) bit_extender_1 (.in(shifter_1_out), .out(bit_extender_1_out));
  Clock clock_1 (.out(clock_1_out));
  RAM #(.addrWidth(5), .dataWidth(32), .bus("separate")) ram_1 (
    .addr(bit_extender_1_out), .din(MemData), .data(MemOut), .str(MemWrite), .clk(clock_1_out),
    .ld(not_1_out), .clr(reset));  // open: sel
  not not_1 (not_1_out, MemWrite);
endmodule

module OUTPUT (
  input  [31:0] Instr,
  input  RegWrite,
  input  [4:0] RegAdr,
  input  [31:0] RegData,
  input  MemWrite,
  input  [6:0] MemAddr_Byte,
  input  [31:0] MemData,
  output [31:0] Instr_2,
  output RegWrite_2,
  output [4:0] RegAddr,
  output [31:0] RegData_2,
  output MemWrite_2,
  output [4:0] MemAddr,
  output [31:0] MemData_2
);

  wire [6:0] shifter_1_out;

  Shifter #(.width(7), .shift("lr")) shifter_1 (.in(MemAddr_Byte), .\dist (3'b010), .out(shifter_1_out));
  Bit_Extender #(.in_width(7), .out_width(5)) bit_extender_1 (.in(shifter_1_out), .out(MemAddr));

  assign Instr_2 = Instr;
  assign MemData_2 = MemData;
  assign MemWrite_2 = MemWrite;
  assign RegAddr = RegAdr;
  assign RegData_2 = RegData;
  assign RegWrite_2 = RegWrite;
endmodule

module zero_EXT_16 (
  input  [15:0] in_1,
  output [31:0] out_2
);

  wire [31:0] bit_extender_1_out;

  assign bit_extender_1_out = {{16{1'b0}}, in_1};  // Bit_Extender bit_extender_1
  Shifter #(.width(32)) shifter_1 (.in(bit_extender_1_out), .\dist (5'b10000), .out(out_2));
endmodule

module signed_EXT_2 (
  input  [15:0] EXT_input,
  output [31:0] EXT_output
);

  wire [15:0] shifter_1_out;

  Shifter #(.width(16)) shifter_1 (.in(EXT_input), .\dist (4'b0010), .out(shifter_1_out));
  assign EXT_output = {{16{shifter_1_out[15]}}, shifter_1_out};  // Bit_Extender bit_extender_1
endmodule
